// Logisim project computer.circ as structural Verilog: 4 circuits, main circuit main
module main (
  input  in_1,
  output [7:0] out_2,
  output [7:0] out_3,
  output [7:0] out_4
);

  wire clock_1_out, cpu_1_membit, not_1_out;
  wire [7:0] cpu_1_datamem, cpu_1_outrom, ram_1_data;
  wire [21:0] rom_1_data;

  ROM #(.dataWidth(22)) rom_1 (.addr(cpu_1_outrom), .data(rom_1_data));  // open: sel
  CPU cpu_1 (
    .instruction(rom_1_data), .inmem(ram_1_data), .reset(in_1), .clk(clock_1_out), .R1(out_3), .R2(out_4),
    .membit(cpu_1_membit), .outROM(cpu_1_outrom), .addrmem(out_2), .datamem(cpu_1_datamem));  // open: outALU
  Clock clock_1 (.out(clock_1_out));
  not not_1 (not_1_out, cpu_1_membit);
  RAM #(.bus("separate")) ram_1 (
    .addr(out_2), .din(cpu_1_datamem), .data(ram_1_data), .str(cpu_1_membit), .clk(clock_1_out),
    .ld(not_1_out), .clr(in_1));  // open: sel

  // Notes on the sheet:
  //   contents of rom_1 (hex, n*v repeats v):
  //   2301 60ff 80001
endmodule

module ALU (
  input  [2:0] control,
  input  [7:0] in1,
  input  [7:0] in2,
  output [7:0] out,
  output Less,
  output Greater,
  output Equal
);

  wire [7:0] adder_1_out, and_1_out, divider_1_out, multiplier_1_out, or_1_out, subtractor_1_out, xor_1_out;

  Adder adder_1 (.a(in1), .b(in2), .out(adder_1_out));  // open: cin, cout
  Subtractor subtractor_1 (.a(in1), .b(in2), .out(subtractor_1_out));  // open: bin, bout
  Multiplier multiplier_1 (.a(in1), .b(in2), .out(multiplier_1_out));  // open: cin, cout
  Divider divider_1 (.a(in1), .b(in2), .out(divider_1_out));  // open: upper, rem
  assign and_1_out = in1 & in2;  // AND_Gate and_1, 8 bits wide
  assign xor_1_out = in1 ^ in2;  // XOR_Gate xor_1, 8 bits wide
  assign or_1_out = in1 | in2;  // OR_Gate or_1, 8 bits wide
  Multiplexer #(.select(3), .width(8)) multiplexer_1 (
    .in0({8{1'b0}}), .in1(adder_1_out), .in2(subtractor_1_out), .in3(multiplier_1_out), .in4(divider_1_out),
    .in5(xor_1_out), .in6(and_1_out), .in7(or_1_out), .out(out), .sel(control));  // open: en
  Comparator comparator_1 (.a(out), .b({8{1'b0}}), .gt(Greater), .eq(Equal), .lt(Less));
endmodule

module CPU (
  input  [21:0] instruction,
  input  [7:0] inmem,
  input  reset,
  input  clk,
  output [7:0] outALU,
  output [7:0] R1,
  output [7:0] R2,
  output membit,
  output [7:0] outROM,
  output [7:0] addrmem,
  output [7:0] datamem
);

  wire cmp_1_out_5, ld1, ld2, ld3, not_1_out, or_1_out;
  wire [2:0] alu_1_less, register_4_q;
  wire [7:0] multiplexer_1_out, multiplexer_2_out, multiplexer_3_out;

  Multiplexer #(.select(3), .width(8)) multiplexer_1 (
    .in0(outALU), .in1(R1), .in2(R2), .in3(addrmem), .in4(instruction[7:0]), .in5(inmem),
    .out(multiplexer_1_out), .sel(instruction[10:8]));  // open: in6, in7, en
  Multiplexer #(.select(2), .width(8)) multiplexer_2 (
    .in0(instruction[7:0]), .in1(R1), .in2(R2), .out(multiplexer_2_out), .sel(instruction[12:11]));  // open: in3, en
  Register register_1 (.D(multiplexer_1_out), .en(ld1), .Q(R1), .clk(clk), .clr(reset));
  Register register_2 (.D(multiplexer_1_out), .en(ld2), .Q(R2), .clk(clk), .clr(reset));
  Register register_3 (.D(multiplexer_1_out), .en(ld3), .Q(addrmem), .clk(clk));  // open: clr
  Multiplexer #(.width(8)) multiplexer_3 (
    .in0(R1), .in1(R2), .out(multiplexer_3_out), .sel(instruction[14]));  // open: en
  not not_1 (not_1_out, cmp_1_out_5);
  ALU alu_1 (
    .control(instruction[17:15]), .in1(multiplexer_3_out), .in2(multiplexer_2_out), .out(outALU),
    .Equal(alu_1_less[2]), .Less(alu_1_less[0]), .Greater(alu_1_less[1]));
  or or_1 (or_1_out, instruction[15], instruction[16], instruction[17]);
  cmp cmp_1 (
    .in_4(instruction[20:18]), .out_5(cmp_1_out_5), .less(register_4_q[0]), .greater(register_4_q[1]),
    .equal(register_4_q[2]));
  Counter SP (
    .load(cmp_1_out_5), .D(instruction[7:0]), .count(not_1_out), .Q(outROM), .clk(clk), .clr(reset));  // open: carry
  Register #(.width(3)) register_4 (.D(alu_1_less), .en(or_1_out), .Q(register_4_q), .clk(clk), .clr(reset));
  Demultiplexer #(.select(2)) demultiplexer_1 (
    .out1(ld1), .out2(ld2), .out3(ld3), .in(1'b1), .sel(instruction[14:13]));  // open: out0, en

  assign datamem = instruction[7:0];
  assign membit = instruction[21];

  // Other names for the same wires on the sheet: alu_out[7:0] = outALU; data[7:0] = instruction[7:0];
  //   regin[2:0] = instruction[10:8]; src[1:0] = instruction[12:11]; save[1:0] = instruction[14:13];
  //   control[2:0] = instruction[17:15]; cmpbits[2:0] = instruction[20:18]; M1[7:0] = addrmem
endmodule

module cmp (
  input  less,
  input  greater,
  input  equal,
  input  [2:0] in_4,
  output out_5
);

  wire and_1_out, and_2_out, and_3_out;

  and and_1 (and_1_out, less, in_4[0]);
  and and_2 (and_2_out, greater, in_4[1]);
  and and_3 (and_3_out, equal, in_4[2]);
  or or_1 (out_5, and_1_out, and_2_out, and_3_out);
endmodule
